# Fritzing sketch components (saved by Fritzing 0.8.3b)
breadboards: 1

parts:
  R1 = Resistor [tolerance=±5% resistance=220 package=THT]
  LED1 = LED - 5mm [color="Red (633nm)" package="5 mm [THT]"]
  S1 = Pushbutton [package="[THT]"]
  Part1 = Arduino Board Ethernet

nets:
  N1: R1.Pin_0, S1.Pin_1, S1.Pin_2, Part1.D2_PWM
  N2: R1.Pin_1, LED1.cathode, Part1.GND
  N3: LED1.anode, Part1.D4
  N4: S1.Pin_3, S1.Pin_4, Part1.5V
