# Fritzing sketch components (saved by Fritzing 0.8.3b)
breadboards: 1

parts:
  Part1 = Electric Imp Breakout  # not connected
  R1 = Resistor [tolerance=±5% resistance=330 package=THT]
  S1 = Pushbutton [package="[THT]"]
  LED1 = LED - 5mm [color="Red (633nm)" package="5 mm [THT]"]

nets:
  N1: R1.Pin_0, LED1.cathode
  N2: S1.Pin_1, S1.Pin_2
  N3: S1.Pin_3, S1.Pin_4

notes:
  5k

custom parts:
  Electric Imp Breakout: Electric Imp Breakout Board with onboard 3.3V regulated power supply
