# Fritzing sketch ez-fritz (saved by Fritzing 0.9.2b)
breadboards: 1

parts:
  Part1 = Arduino Yun
  R2 = Resistor [tolerance=±5% resistance=10k package=THT]
  S1 = Pushbutton [package="[THT]"]
  LED1 = LED - 5mm [color="Red (633nm)" package="5 mm [THT]"]
  R1 = Resistor [tolerance=±5% resistance=10k package=THT]

nets:
  N1: Part1.5V, S1.Pin_3, S1.Pin_4
  N2: Part1.GND, R2.Pin_1, LED1.cathode
  N3: Part1.D5_PWM, R2.Pin_0, S1.Pin_1, S1.Pin_2
  N4: Part1.D7, R1.Pin_1
  N5: LED1.anode, R1.Pin_0
